# Fritzing sketch automatic-plant-watering-system_Fritzing (saved by Fritzing 0.9.3b)
breadboards: 1

parts:
  Part1 = Arduino Mega 2560 (Rev3)
  Part2 = LCD Keypad Shield
  Part3 = KY-019 5V Relay Module [package="Breakout board"]
  Part4 = KY-019 5V Relay Module [package="Breakout board"]
  M2 = DC Motor
  M1 = DC Motor

nets:
  N1: Part1.D22, Part3.S
  N2: Part1.D28, Part4.S
  N3: Part2.+5V, Part3.+, Part4.+
  N4: Part2.GND, Part3.-, Part4.-
  N5: Part3.Common, M1.pin_1
  N6: Part4.Common, M2.pin_1

notes:
  External USB power supply

custom parts:
  LCD Keypad Shield: It consists of a 1602 white character blue backlight LCD. The keypad consists of 5 keys — select, up, right, down and left. To save the digital IO pins, the keypad interface uses only one ADC channel. The key value is read through a 5 stage voltage divider.
  KY-019 5V Relay Module: KY-019 5V Relay module, used to control AC circuits.
